// Logisim project gate.circ as structural Verilog: 1 circuit, main circuit main
module main (
  input  A,
  input  B,
  input  C
);

  wire and_1_out, not_1_out, or_1_out;

  not not_1 (not_1_out, A);
  or or_1 (or_1_out, B, C);
  and and_1 (and_1_out, not_1_out, or_1_out);
  LED led_1 (.in(and_1_out));
endmodule
