// Logisim project gates.circ as structural Verilog: 1 circuit, main circuit main
module main (
  input  in_1,
  input  in_2,
  input  in_3,
  input  in_4,
  input  in_5,
  input  in_6
);

  wire and_1_out, buffer_1_out, not_1_out, or_1_out;

  and and_1 (and_1_out, in_1, in_3);
  not not_1 (not_1_out, in_5);
  buf buffer_1 (buffer_1_out, in_6);
  LED led_1 (.in(and_1_out));
  LED led_2 (.in(not_1_out));
  LED led_3 (.in(buffer_1_out));
  or or_1 (or_1_out, in_2, in_4);
  LED led_4 (.in(or_1_out));
endmodule
